# Fritzing sketch 3-led-indicator (saved by Fritzing 0.9.3b)
breadboards: 1

parts:
  Part1 = INMP441
  A1 = XIAO ESP32C3-smd
  LED1 = smd LED [color="Red (633nm)" package="0603 [SMD]"]
  LED2 = smd LED [color="Green (555nm)" package="0603 [SMD]"]
  LED3 = smd LED [color="Yellow (595nm)" package="0603 [SMD]"]
  R1 = Resistor [tolerance=±5% resistance=100 package=THT]
  R2 = Resistor [tolerance=±5% resistance=100 package=THT]
  R3 = Resistor [tolerance=±5% resistance=100 package=THT]

nets:
  N1: Part1.WS, A1.Pin_11
  N2: Part1.SCK, A1.Pin_10
  N3: Part1.SD, A1.Pin_9
  N4: Part1.VDD, A1.Pin_20, R1.Pin_0, R2.Pin_0, R3.Pin_0
  N5: Part1.GND, A1.Pin_2, A1.Pin_21
  N6: A1.Pin_13, LED2.anode
  N7: A1.Pin_14, LED3.anode
  N8: A1.Pin_15, LED1.anode
  N9: LED1.cathode, R3.Pin_1
  N10: LED2.cathode, R1.Pin_1
  N11: LED3.cathode, R2.Pin_1

custom parts:
  INMP441: This is a simple breakout board for the INMP441 I2S MEMS microphone.
  XIAO ESP32C3-smd: Seeed Studio XIAO ESP32C3 adopts new RISC-V architecture, supporting both Wi-Fi and BLE wireless connectivities.
